// Logisim project core1.circ as structural Verilog: 8 circuits, main circuit ALU
module Unidade_Processamento (
  input  [3:0] c,
  input  [3:0] b,
  input  [3:0] a,
  input  [1:0] SM,
  input  SD,
  input  SR,
  input  ER,
  input  CLK,
  input  SA,
  input  SB,
  input  SnA,
  output [3:0] R___a___b___c
);

  wire decoder_1_out0, decoder_1_out1;
  wire [3:0] alu_1_r, multiplexer_1_out, multiplexer_2_out, multiplexer_4_out, reg_1_data_o, reg_2_data_o;

  Decoder #(.disabled(0)) decoder_1 (.out0(decoder_1_out0), .out1(decoder_1_out1), .sel(SR), .en(ER));
  Multiplexer #(.select(2), .width(4), .disabled(0), .enable("false")) multiplexer_1 (
    .in0(a), .in1(b), .in2(c), .out(multiplexer_1_out), .sel(SM));  // open: in3
  Multiplexer #(.width(4), .disabled(0), .enable("false")) multiplexer_2 (
    .in0(multiplexer_1_out), .in1(alu_1_r), .out(multiplexer_2_out), .sel(SD));
  REG reg_1 (.Data_i(multiplexer_2_out), .E(decoder_1_out0), .CLK(CLK), .Data_o(reg_1_data_o), .CLR(1'b0));
  Multiplexer #(.width(4), .disabled(0), .enable("false")) multiplexer_3 (
    .in0(reg_1_data_o), .in1(reg_2_data_o), .out(R___a___b___c), .sel(SA));
  ALU alu_1 (.A(R___a___b___c), .B(multiplexer_4_out), .SnA(SnA), .R(alu_1_r));  // open: CyBw, Z
  REG reg_2 (.Data_i(multiplexer_2_out), .E(decoder_1_out1), .CLK(CLK), .Data_o(reg_2_data_o), .CLR(1'b0));
  Multiplexer #(.width(4), .disabled(0), .enable("false")) multiplexer_4 (
    .in0(reg_1_data_o), .in1(reg_2_data_o), .out(multiplexer_4_out), .sel(SB));

  // Notes on the sheet:
  //   RA
  //   RB
endmodule

module Unidade_Controlo (
  input  Reset,
  input  MCLK,
  output [1:0] SM,
  output SD,
  output ER,
  output SR,
  output SA,
  output SB,
  output SnA,
  output [3:0] out_10
);

  wire not_1_out;
  wire [3:0] rom_1_data;

  not not_1 (not_1_out, MCLK);
  // Probe on rom_1_data
  REG reg_1 (.Data_i(rom_1_data), .E(1'b1), .CLK(not_1_out), .Data_o(out_10), .CLR(Reset));
  // Probe on out_10
  ROM #(.addrWidth(4), .dataWidth(12)) rom_1 (
    .addr(out_10), .data({rom_1_data, SM, SD, ER, SR, SA, SB, SnA}), .sel(1'b1));

  // Notes on the sheet:
  //   contents of rom_1 (hex, n*v repeats v):
  //   110 258 332 498 533 500
endmodule

module Register_File (
  input  [3:0] in_1,
  input  SR,
  input  ER,
  input  CLK,
  input  SA,
  input  SB,
  output [3:0] out_7,
  output [3:0] out_8,
  output [3:0] out_9,
  output [3:0] out_10
);

  wire decoder_1_out0, decoder_1_out1;

  Decoder #(.disabled(0)) decoder_1 (.out0(decoder_1_out0), .out1(decoder_1_out1), .sel(SR), .en(ER));
  REG reg_1 (.Data_i(in_1), .E(decoder_1_out0), .CLK(CLK), .Data_o(out_8), .CLR(1'b0));
  Multiplexer #(.width(4), .disabled(0), .enable("false")) multiplexer_1 (
    .in0(out_8), .in1(out_7), .out(out_9), .sel(SA));
  REG reg_2 (.Data_i(in_1), .E(decoder_1_out1), .CLK(CLK), .Data_o(out_7), .CLR(1'b0));
  Multiplexer #(.width(4), .disabled(0), .enable("false")) multiplexer_2 (
    .in0(out_8), .in1(out_7), .out(out_10), .sel(SB));

  // Notes on the sheet:
  //   RA
  //   RB
endmodule

module CPU (
  input  [3:0] c,
  input  [3:0] b,
  input  [3:0] a,
  input  MCLK,
  output [3:0] R___a___b___c,
  output [3:0] out_6
);

  wire not_1_out, Reset_out;
  wire [3:0] alu_1_r, multiplexer_1_out, multiplexer_2_out, reg_1_data_o, register_file_1_out_7,
       register_file_1_out_8, rom_1_data_2;
  wire [7:0] rom_1_data;

  Button Reset (.out(Reset_out));
  not not_1 (not_1_out, MCLK);
  // Probe on rom_1_data_2
  REG reg_1 (.Data_i(rom_1_data_2), .E(1'b1), .CLK(not_1_out), .Data_o(reg_1_data_o), .CLR(Reset_out));
  // Probe on reg_1_data_o
  ROM #(.addrWidth(4), .dataWidth(12)) rom_1 (.addr(reg_1_data_o), .data({rom_1_data_2, rom_1_data}), .sel(1'b1));
  Multiplexer #(.select(2), .width(4), .disabled(0), .enable("false")) multiplexer_1 (
    .in0(a), .in1(b), .in2(c), .out(multiplexer_1_out), .sel(rom_1_data[7:6]));  // open: in3
  // Probe on multiplexer_1_out
  // Probe on register_file_1_out_8
  // Probe on register_file_1_out_7
  Multiplexer #(.width(4), .disabled(0), .enable("false")) multiplexer_2 (
    .in0(multiplexer_1_out), .in1(alu_1_r), .out(multiplexer_2_out), .sel(rom_1_data[5]));
  // Probe on multiplexer_2_out
  Register_File register_file_1 (
    .ER(rom_1_data[3]), .SR(rom_1_data[4]), .SA(rom_1_data[2]), .SB(rom_1_data[1]), .CLK(MCLK),
    .in_1(multiplexer_2_out), .out_7(register_file_1_out_7), .out_8(register_file_1_out_8),
    .out_9(R___a___b___c), .out_10(out_6));
  ALU alu_1 (.A(R___a___b___c), .B(out_6), .SnA(rom_1_data[0]), .R(alu_1_r));  // open: CyBw, Z

  // Notes on the sheet:
  //   contents of rom_1 (hex, n*v repeats v):
  //   110 258 332 498 533 500
  //   SM
  //   SD
  //   SR
  //   ER
  //   SA
  //   SB
  //   SnA
endmodule

module ALU (
  input  [3:0] A,
  input  [3:0] B,
  input  SnA,
  output [3:0] R,
  output Z,
  output CyBw
);

  wire adder_1_cout;
  wire [3:0] xor_1_out;

  xor xor_1 (xor_1_out[0], B[0], SnA);
  xor xor_2 (xor_1_out[1], B[1], SnA);
  xor xor_3 (xor_1_out[2], B[2], SnA);
  xor xor_4 (xor_1_out[3], B[3], SnA);
  Adder #(.width(4)) adder_1 (.a(A), .b(xor_1_out), .out(R), .cin(SnA), .cout(adder_1_cout));
  xor xor_5 (CyBw, adder_1_cout, SnA);
  nor nor_1 (Z, R[0], R[1], R[2], R[3]);
endmodule

module D_E (
  input  in_1,
  input  D,
  input  E,
  input  CLR,
  output Q
);

  wire multiplexer_1_out;

  Multiplexer #(.disabled(0), .enable("false")) multiplexer_1 (.in0(Q), .in1(D), .out(multiplexer_1_out), .sel(E));
  D_Flip_Flop d_ff_1 (.clk(in_1), .D(multiplexer_1_out), .Q(Q), .preset(1'b0), .en(1'b1), .reset(CLR));  // open: Qn
endmodule

module REG (
  input  [3:0] Data_i,
  input  CLR,
  input  E,
  input  CLK,
  output [3:0] Data_o
);

  D_E d_e_1 (.in_1(CLK), .D(Data_i[3]), .E(E), .Q(Data_o[3]), .CLR(CLR));
  D_E d_e_2 (.in_1(CLK), .D(Data_i[2]), .E(E), .Q(Data_o[2]), .CLR(CLR));
  D_E d_e_3 (.in_1(CLK), .D(Data_i[1]), .E(E), .Q(Data_o[1]), .CLR(CLR));
  D_E d_e_4 (.in_1(CLK), .D(Data_i[0]), .E(E), .Q(Data_o[0]), .CLR(CLR));
endmodule

module RAM (
  input  ld,
  input  [2:0] A0_2,
  input  str,
  input  Sel,
  input  [3:0] D0_3,
  input  CLK,
  output [3:0] D0_3_2
);

  wire and_1_out, and_2_out, decoder_1_out0, decoder_1_out1, decoder_1_out2, decoder_1_out3, decoder_1_out4,
       decoder_1_out5, decoder_1_out6, decoder_1_out7;
  wire [3:0] reg_1_data_o, reg_2_data_o, reg_3_data_o, reg_4_data_o, reg_5_data_o, reg_6_data_o,
       reg_7_data_o, reg_8_data_o;

  and and_1 (and_1_out, ld, Sel);
  and and_2 (and_2_out, str, Sel);
  Decoder #(.select(3), .disabled(0)) decoder_1 (
    .out0(decoder_1_out0), .out1(decoder_1_out1), .out2(decoder_1_out2), .out3(decoder_1_out3),
    .out4(decoder_1_out4), .out5(decoder_1_out5), .out6(decoder_1_out6), .out7(decoder_1_out7), .sel(A0_2),
    .en(and_2_out));
  REG reg_1 (.Data_i(D0_3), .E(decoder_1_out0), .CLK(CLK), .Data_o(reg_1_data_o));  // open: CLR
  REG reg_2 (.Data_i(D0_3), .E(decoder_1_out1), .CLK(CLK), .Data_o(reg_2_data_o));  // open: CLR
  REG reg_3 (.Data_i(D0_3), .E(decoder_1_out2), .CLK(CLK), .Data_o(reg_3_data_o));  // open: CLR
  REG reg_4 (.Data_i(D0_3), .E(decoder_1_out3), .CLK(CLK), .Data_o(reg_4_data_o));  // open: CLR
  REG reg_5 (.Data_i(D0_3), .E(decoder_1_out4), .CLK(CLK), .Data_o(reg_5_data_o));  // open: CLR
  REG reg_6 (.Data_i(D0_3), .E(decoder_1_out5), .CLK(CLK), .Data_o(reg_6_data_o));  // open: CLR
  REG reg_7 (.Data_i(D0_3), .E(decoder_1_out6), .CLK(CLK), .Data_o(reg_7_data_o));  // open: CLR
  REG reg_8 (.Data_i(D0_3), .E(decoder_1_out7), .CLK(CLK), .Data_o(reg_8_data_o));  // open: CLR
  // Probe on reg_1_data_o
  // Probe on reg_2_data_o
  // Probe on reg_3_data_o
  // Probe on reg_4_data_o
  // Probe on reg_5_data_o
  // Probe on reg_6_data_o
  // Probe on reg_7_data_o
  // Probe on reg_8_data_o
  Multiplexer #(.select(3), .width(4)) multiplexer_1 (
    .in0(reg_1_data_o), .in1(reg_2_data_o), .in2(reg_3_data_o), .in3(reg_4_data_o), .in4(reg_5_data_o),
    .in5(reg_6_data_o), .in6(reg_7_data_o), .in7(reg_8_data_o), .out(D0_3_2), .sel(A0_2), .en(and_1_out));

  // Notes on the sheet:
  //   0
  //   1
  //   2
  //   3
  //   4
  //   5
  //   6
  //   7
endmodule
