// Logisim project core5.circ as structural Verilog: 7 circuits, main circuit Unidade Funcional
module Unidade_Funcional (
  input  [7:0] PC,
  input  [7:0] Data_Bus,
  input  [2:0] const3,
  input  [1:0] SD,
  input  [1:0] AD,
  input  ER,
  input  [1:0] AB,
  input  OP_ALU,
  input  EP,
  input  CLK,
  input  WR,
  input  SA,
  output [7:0] Data_Bus_2,
  output [7:0] Address_Bus,
  output Z,
  output C
);

  wire [1:0] alu_1_z;
  wire [7:0] alu_1_r, bit_extender_1_out, multiplexer_1_out, register_file_1_a, register_file_1_b,
       register_file_1_out_7, register_file_1_out_8, register_file_1_out_9, register_file_1_out_10;

  assign bit_extender_1_out = {{5{1'b0}}, const3};  // Bit_Extender bit_extender_1
  Multiplexer #(.select(2), .width(8), .disabled(0), .enable("false")) multiplexer_1 (
    .in0(bit_extender_1_out), .in1(Data_Bus), .in2(alu_1_r), .out(multiplexer_1_out), .sel(SD));  // open: in3
  // Probe on register_file_1_out_10
  Register_File register_file_1 (
    .in_1(multiplexer_1_out), .CLK(CLK), .ER(ER), .AD(AD), .AA(AD), .AB(AB), .A(register_file_1_a),
    .B(register_file_1_b), .out_7(register_file_1_out_7), .out_8(register_file_1_out_8),
    .out_9(register_file_1_out_9), .out_10(register_file_1_out_10));
  // Probe on register_file_1_out_9
  // Probe on register_file_1_out_8
  // Probe on register_file_1_out_7
  Register #(.width(2)) PSW (.D(alu_1_z), .en(EP), .Q({C, Z}), .clk(CLK), .clr(1'b1));
  ALU alu_1 (
    .A(register_file_1_a), .B(register_file_1_b), .SnA(OP_ALU), .R(alu_1_r), .Z(alu_1_z[0]), .CyBw(alu_1_z[1]));
  assign Data_Bus = WR ? register_file_1_a : 8'bz;  // Controlled_Buffer controlled_buffer_1
  Multiplexer #(.width(8), .enable("false")) multiplexer_2 (
    .in0(PC), .in1(register_file_1_b), .out(Address_Bus), .sel(SA));

  assign Data_Bus_2 = Data_Bus;
endmodule

module Register_File (
  input  [7:0] in_1,
  input  CLK,
  input  ER,
  input  [1:0] AD,
  input  [1:0] AA,
  input  [1:0] AB,
  output [7:0] out_7,
  output [7:0] out_8,
  output [7:0] out_9,
  output [7:0] out_10,
  output [7:0] A,
  output [7:0] B
);

  wire decoder_1_out0, decoder_1_out1, decoder_1_out2, decoder_1_out3;

  Decoder #(.select(2), .disabled(0)) decoder_1 (
    .out0(decoder_1_out0), .out1(decoder_1_out1), .out2(decoder_1_out2), .out3(decoder_1_out3), .sel(AD),
    .en(ER));
  Register register_1 (.D(in_1), .en(decoder_1_out3), .Q(out_7), .clk(CLK), .clr(1'b0));
  Register register_2 (.D(in_1), .en(decoder_1_out2), .Q(out_8), .clk(CLK), .clr(1'b0));
  Register register_3 (.D(in_1), .en(decoder_1_out1), .Q(out_9), .clk(CLK), .clr(1'b0));
  Register register_4 (.D(in_1), .en(decoder_1_out0), .Q(out_10), .clk(CLK), .clr(1'b0));
  Multiplexer #(.select(2), .width(8), .disabled(0), .enable("false")) multiplexer_1 (
    .in0(out_10), .in1(out_9), .in2(out_8), .in3(out_7), .out(A), .sel(AA));
  Multiplexer #(.select(2), .width(8), .disabled(0), .enable("false")) multiplexer_2 (
    .in0(out_10), .in1(out_9), .in2(out_8), .in3(out_7), .out(B), .sel(AB));
endmodule

module Unidade_Controlo (
  input  [7:0] in_1,
  input  Reset,
  input  MCLK,
  input  Z,
  input  C,
  output [2:0] out_6,
  output [1:0] out_7,
  output [1:0] out_8,
  output out_9,
  output out_10,
  output out_11,
  output out_12,
  output out_13,
  output [1:0] out_14,
  output out_15,
  output [7:0] out_16,
  output out_17
);

  wire EIR, EPC, nCLK, SO, ST;
  wire [4:0] offset5;
  wire [7:0] adder_1_out, bit_extender_1_out, IR_q, multiplexer_1_out;

  ASM asm_1 (.MCLK(MCLK), .CLR(Reset), .ST(ST), .CLK(out_17), .nCLK(nCLK));
  Multiplexer #(.width(8), .enable("false")) multiplexer_1 (
    .in0(8'h1), .in1(bit_extender_1_out), .out(multiplexer_1_out), .sel(SO));
  assign bit_extender_1_out = {{3{offset5[4]}}, offset5};  // Bit_Extender bit_extender_1
  Adder adder_1 (.a(out_16), .b(multiplexer_1_out), .out(adder_1_out), .cin(1'b0));  // open: cout
  Register PC (.D(adder_1_out), .en(EPC), .Q(out_16), .clk(nCLK), .clr(Reset));
  Instruction_Decoder instruction_decoder_1 (
    .\Instrução (IR_q), .offset5(offset5), .AD(out_8), .AB(out_7), .WR(out_11), .RD(out_10), .SD(out_14),
    .ER(out_13), .EP(out_12), .Z(Z), .C(C), .SO(SO), .const3(out_6), .ST(ST), .EIR(EIR), .SA(out_15),
    .EPC(EPC), .OP_ALU(out_9));
  Register IR (.D(in_1), .en(EIR), .Q(IR_q), .clk(out_17), .clr(1'b0));

  // Other names for the same wires on the sheet: AB[1:0] = out_7; AD[1:0] = out_8; CLK = out_17; const3[2:0] = out_6;
  //   EP = out_12; ER = out_13; OP_ALU = out_9; PC[7:0] = out_16; RD = out_10; RST = Reset; SA = out_15;
  //   SD[1:0] = out_14; WR = out_11

  // Notes on the sheet:
  //   Instruction Decoder
endmodule

module ALU (
  input  [7:0] A,
  input  [7:0] B,
  input  SnA,
  output [7:0] R,
  output Z,
  output CyBw
);

  wire adder_1_cout, subtractor_1_bout;
  wire [7:0] adder_1_out, subtractor_1_out;

  Adder adder_1 (.a(A), .b(B), .out(adder_1_out), .cin(1'b0), .cout(adder_1_cout));
  Subtractor subtractor_1 (.a(A), .b(B), .out(subtractor_1_out), .bin(1'b0), .bout(subtractor_1_bout));
  Multiplexer #(.width(8), .disabled(0), .enable("false")) multiplexer_1 (
    .in0(adder_1_out), .in1(subtractor_1_out), .out(R), .sel(SnA));
  Multiplexer #(.disabled(0), .enable("false")) multiplexer_2 (
    .in0(adder_1_cout), .in1(subtractor_1_bout), .out(CyBw), .sel(SnA));
  and and_1 (Z, ~R[0], ~R[1], ~R[2], ~R[3], ~R[4], ~R[5], ~R[6], ~R[7]);  // AND_Gate
endmodule

module Instruction_Decoder (
  input  [7:0] \Instrução ,
  input  C,
  input  Z,
  input  ST,
  output [4:0] offset5,
  output [1:0] AD,
  output [1:0] AB,
  output [2:0] const3,
  output OP_ALU,
  output WR,
  output RD,
  output [1:0] SD,
  output ER,
  output EP,
  output SO,
  output EIR,
  output SA,
  output EPC
);

  ROM #(.addrWidth(6), .dataWidth(10)) rom_1 (
    .addr({\Instrução [7:5], C, Z, ST}), .data({EPC, SA, EIR, SO, EP, ER, SD, RD, WR}), .sel(1'b1));

  assign AB = \Instrução [3:2];
  assign AD = \Instrução [1:0];
  assign const3 = \Instrução [4:2];
  assign offset5 = \Instrução [4:0];
  assign OP_ALU = \Instrução [5];

  // Notes on the sheet:
  //   contents of rom_1 (hex, n*v repeats v):
  //   82 210 82 210 82 210 82 210 82 316 82 316 82 316 82 316 82 240 82 240 82 200 82 200 82 301 82 301 82
  //   301 82 301 82 238 82 238 82 238 82 238 82 238 82 238 82 238 82 238 82 200 82 240 82 200 82 240 82
  //   240 82 240 82 240 82 240
endmodule

module CPU (
);

  wire CLK, EIR, EP, EPC, ER, MCLK_out, nCLK, OP_ALU, or_1_out, RD, RST, SA, SO, ST, WR;
  wire [1:0] AB, AD, alu_1_z, PSW_q, SD;
  wire [2:0] const3;
  wire [4:0] offset5;
  wire [7:0] adder_1_out, alu_1_r, bit_extender_1_out, bit_extender_2_out, controlled_buffer_1_out, IR_q,
       multiplexer_1_out, multiplexer_2_out, multiplexer_3_out, PC, register_file_1_a, register_file_1_b,
       register_file_1_out_7, register_file_1_out_8, register_file_1_out_9, register_file_1_out_10;

  Button Reset (.out(RST));
  Clock MCLK (.out(MCLK_out));
  ASM asm_1 (.MCLK(MCLK_out), .CLR(RST), .ST(ST), .CLK(CLK), .nCLK(nCLK));
  assign bit_extender_1_out = {{3{offset5[4]}}, offset5};  // Bit_Extender bit_extender_1
  // Probe on ST
  // Probe on CLK
  // Probe on nCLK
  Adder adder_1 (.a(PC), .b(multiplexer_1_out), .out(adder_1_out), .cin(1'b0));  // open: cout
  Multiplexer #(.width(8), .enable("false")) multiplexer_1 (
    .in0(8'h1), .in1(bit_extender_1_out), .out(multiplexer_1_out), .sel(SO));
  Register u_PC (.D(adder_1_out), .en(EPC), .Q(PC), .clk(nCLK), .clr(RST));
  Instruction_Decoder instruction_decoder_1 (
    .\Instrução (IR_q), .offset5(offset5), .AD(AD), .AB(AB), .WR(WR), .RD(RD), .SD(SD), .ER(ER), .EP(EP),
    .Z(PSW_q[0]), .C(PSW_q[1]), .SO(SO), .const3(const3), .ST(ST), .EIR(EIR), .SA(SA), .EPC(EPC),
    .OP_ALU(OP_ALU));
  Register IR (.D(controlled_buffer_1_out), .en(EIR), .Q(IR_q), .clk(CLK), .clr(RST));
  // Probe on IR_q
  assign bit_extender_2_out = {{5{1'b0}}, const3};  // Bit_Extender bit_extender_2
  // Probe on AD
  // Probe on AB
  Multiplexer #(.select(2), .width(8), .disabled(0), .enable("false")) multiplexer_2 (
    .in0(bit_extender_2_out), .in1(controlled_buffer_1_out), .in2(alu_1_r), .out(multiplexer_2_out), .sel(SD));  // open: in3
  // Probe on multiplexer_2_out
  // Probe on register_file_1_out_10
  Register_File register_file_1 (
    .in_1(multiplexer_2_out), .CLK(CLK), .ER(ER), .AD(AD), .AA(AD), .AB(AB), .A(register_file_1_a),
    .B(register_file_1_b), .out_7(register_file_1_out_7), .out_8(register_file_1_out_8),
    .out_9(register_file_1_out_9), .out_10(register_file_1_out_10));
  // Probe on register_file_1_out_9
  // Probe on register_file_1_out_8
  // Probe on register_file_1_out_7
  Register #(.width(2)) PSW (.D(alu_1_z), .en(EP), .Q(PSW_q), .clk(CLK), .clr(1'b0));
  ALU alu_1 (
    .A(register_file_1_a), .B(register_file_1_b), .SnA(OP_ALU), .R(alu_1_r), .Z(alu_1_z[0]), .CyBw(alu_1_z[1]));
  // Probe on PSW_q[1]
  // Probe on PSW_q[0]
  assign controlled_buffer_1_out = WR ? register_file_1_a : 8'bz;  // Controlled_Buffer controlled_buffer_1
  // Probe on controlled_buffer_1_out
  // Probe on multiplexer_3_out
  Multiplexer #(.width(8), .disabled(0), .enable("false")) multiplexer_3 (
    .in0(PC), .in1(register_file_1_b), .out(multiplexer_3_out), .sel(SA));
  // Probe on SA
  or or_1 (or_1_out, WR, RD);
  RAM ram_1 (.addr(multiplexer_3_out), .data(controlled_buffer_1_out), .sel(or_1_out), .clk(CLK), .ld(RD), .clr(1'b0));

  // Notes on the sheet:
  //   Instruction Decoder
  //   Memory
endmodule

module ASM (
  input  MCLK,
  input  CLR,
  output nCLK,
  output CLK,
  output ST
);

  not not_1 (nCLK, MCLK);
  T_Flip_Flop t_ff_1 (.clk(MCLK), .T(1'b1), .Q(ST), .reset(CLR), .en(1'b1));  // open: Qn, preset

  assign CLK = MCLK;
endmodule
