// Logisim project core2.circ as structural Verilog: 8 circuits, main circuit ALU
module Unidade_Processamento (
  input  [3:0] Data,
  input  [3:0] IMM4,
  input  [1:0] SD,
  input  SR,
  input  ER,
  input  CLK,
  input  SA,
  input  SB,
  input  SnA,
  output [3:0] Address,
  output [3:0] Data_2,
  output Cy
);

  wire alu_1_cy, decoder_1_out0, decoder_1_out1;
  wire [3:0] alu_1_r, multiplexer_1_out, reg_1_data_o, reg_2_data_o;

  Decoder #(.disabled(0)) decoder_1 (.out0(decoder_1_out0), .out1(decoder_1_out1), .sel(SR), .en(ER));
  REG reg_1 (
    .Data_i(multiplexer_1_out), .E(decoder_1_out0), .CLK(CLK), .Data_o(reg_1_data_o), .CLR(1'b0));  // open: out_5
  Multiplexer #(.select(2), .width(4), .disabled(0), .enable("false")) multiplexer_1 (
    .in0(IMM4), .in1(Data), .in2(alu_1_r), .out(multiplexer_1_out), .sel(SD));  // open: in3
  Multiplexer #(.width(4), .disabled(0), .enable("false")) multiplexer_2 (
    .in0(reg_1_data_o), .in1(reg_2_data_o), .out(Data_2), .sel(SA));
  ALU alu_1 (.Cy(alu_1_cy), .A(Data_2), .B(Address), .SnA(SnA), .R(alu_1_r));  // open: Z
  D_E d_e_1 (.in_1(CLK), .D(alu_1_cy), .E(1'b1), .Q(Cy), .CLR(1'b0));
  REG reg_2 (
    .Data_i(multiplexer_1_out), .E(decoder_1_out1), .CLK(CLK), .Data_o(reg_2_data_o), .CLR(1'b0));  // open: out_5
  Multiplexer #(.width(4), .disabled(0), .enable("false")) multiplexer_3 (
    .in0(reg_1_data_o), .in1(reg_2_data_o), .out(Address), .sel(SB));

  // Notes on the sheet:
  //   RA
  //   RB
endmodule

module Unidade_Controlo (
  input  Reset,
  input  MCLK,
  input  CY,
  output [3:0] IMM4,
  output [1:0] SD,
  output SR,
  output ER,
  output SnA,
  output WR,
  output RD
);

  wire not_1_out;
  wire [3:0] reg_1_data_o, rom_1_data;

  not not_1 (not_1_out, MCLK);
  REG reg_1 (.Data_i(rom_1_data), .E(1'b1), .CLK(not_1_out), .Data_o(reg_1_data_o), .CLR(Reset));  // open: out_5
  ROM #(.addrWidth(5), .dataWidth(15)) rom_1 (
    .addr({reg_1_data_o, CY}), .data({rom_1_data, IMM4, SD, SR, ER, SnA, WR, RD}), .sel(1'b1));

  // Notes on the sheet:
  //   contents of rom_1 (hex, n*v repeats v):
  //   818 818 1031 1031 1898 1898 2039 2039 2850 2850 3118 3118 3839 3839 4054 4054 4998 4998 5002 5002
  //   5000 5000
endmodule

module Register_File (
  input  [3:0] in_1,
  input  SR,
  input  ER,
  input  CLK,
  input  SA,
  input  SB,
  output [3:0] out_7,
  output [3:0] out_8,
  output [3:0] out_9,
  output [3:0] out_10
);

  wire decoder_1_out0, decoder_1_out1;

  Decoder #(.disabled(0)) decoder_1 (.out0(decoder_1_out0), .out1(decoder_1_out1), .sel(SR), .en(ER));
  REG reg_1 (.Data_i(in_1), .E(decoder_1_out0), .CLK(CLK), .Data_o(out_8), .CLR(1'b0));  // open: out_5
  Multiplexer #(.width(4), .disabled(0), .enable("false")) multiplexer_1 (
    .in0(out_8), .in1(out_7), .out(out_9), .sel(SA));
  REG reg_2 (.Data_i(in_1), .E(decoder_1_out1), .CLK(CLK), .Data_o(out_7), .CLR(1'b0));  // open: out_5
  Multiplexer #(.width(4), .disabled(0), .enable("false")) multiplexer_2 (
    .in0(out_8), .in1(out_7), .out(out_10), .sel(SB));

  // Notes on the sheet:
  //   RA
  //   RB
endmodule

module CPU (
  input  MCLK,
  output [3:0] out_2,
  output [3:0] out_3
);

  wire alu_1_cy, not_1_out, not_2_out, Reset_out;
  wire [0:0] d_e_1_q;
  wire [3:0] alu_1_r, multiplexer_1_out, ram_1_data, reg_1_data_o, reg_1_out_5, register_file_1_out_9,
       register_file_1_out_10, rom_1_data_2;
  wire [11:0] rom_1_data;

  Button Reset (.out(Reset_out));
  REG reg_1 (
    .Data_i(rom_1_data_2), .E(1'b1), .CLK(not_1_out), .Data_o(reg_1_data_o), .CLR(Reset_out),
    .out_5(reg_1_out_5));
  not not_1 (not_1_out, MCLK);
  // Probe on reg_1_out_5
  ROM #(.addrWidth(5), .dataWidth(16)) rom_1 (
    .addr({reg_1_data_o, d_e_1_q[0]}), .data({rom_1_data_2, rom_1_data}), .sel(1'b1));
  // Probe on rom_1_data[7:6]
  Multiplexer #(.select(2), .width(4), .disabled(0), .enable("false")) multiplexer_1 (
    .in0(rom_1_data[11:8]), .in1(ram_1_data), .in2(alu_1_r), .out(multiplexer_1_out), .sel(rom_1_data[7:6]));  // open: in3
  // Probe on multiplexer_1_out
  Register_File register_file_1 (
    .ER(rom_1_data[4]), .SR(rom_1_data[5]), .CLK(MCLK), .SA(rom_1_data[3]), .SB(rom_1_data[2]),
    .in_1(multiplexer_1_out), .out_9(register_file_1_out_9), .out_10(register_file_1_out_10), .out_7(out_3),
    .out_8(out_2));
  ALU alu_1 (
    .Cy(alu_1_cy), .A(register_file_1_out_9), .B(register_file_1_out_10), .SnA(rom_1_data[1]), .R(alu_1_r));  // open: Z
  D_E d_e_1 (.in_1(MCLK), .D(alu_1_cy), .E(1'b1), .Q(d_e_1_q[0]), .CLR(1'b0));
  // Probe on ram_1_data
  // Probe on register_file_1_out_10
  // Probe on register_file_1_out_9
  not not_2 (not_2_out, rom_1_data[0]);
  RAM_part #(.addrWidth(4), .dataWidth(4), .bus("separate")) ram_1 (
    .addr(register_file_1_out_10), .din(register_file_1_out_9), .data(ram_1_data), .str(not_2_out),
    .sel(1'b1), .clk(MCLK), .ld(rom_1_data[0]), .clr(1'b0));

  // Notes on the sheet:
  //   contents of rom_1 (hex, n*v repeats v):
  //   40d 40d 815 815 c4d c4d 101d 101d 1423 3c23 188d 188d 1c00 1c00 204d 204d 2415 2415 280d 280d 2c00
  //   2c00 308d 308d 3415 3415 384d 384d 3c00 3c00 3c01 3c01
  //   IMM4
  //   SD
  //   SR
  //   ER
  //   SA
  //   SB
  //   SnA
  //   RnW
  //   CY
endmodule

module ALU (
  input  [3:0] A,
  input  [3:0] B,
  input  SnA,
  output [3:0] R,
  output Z,
  output Cy
);

  wire adder_1_cout;
  wire [3:0] xor_1_out;

  xor xor_1 (xor_1_out[0], B[0], SnA);
  xor xor_2 (xor_1_out[1], B[1], SnA);
  xor xor_3 (xor_1_out[2], B[2], SnA);
  xor xor_4 (xor_1_out[3], B[3], SnA);
  Adder #(.width(4)) adder_1 (.a(A), .b(xor_1_out), .out(R), .cin(SnA), .cout(adder_1_cout));
  xor xor_5 (Cy, adder_1_cout, SnA);
  and and_1 (Z, ~R[0], ~R[1], ~R[2], ~R[3]);  // AND_Gate

  // Notes on the sheet:
  //   Cy: pull=up
  //   R: pull=up
  //   Z: pull=up
endmodule

module D_E (
  input  in_1,
  input  D,
  input  E,
  input  CLR,
  output Q
);

  wire multiplexer_1_out;

  Multiplexer #(.disabled(0), .enable("false")) multiplexer_1 (.in0(Q), .in1(D), .out(multiplexer_1_out), .sel(E));
  D_Flip_Flop d_ff_1 (.clk(in_1), .D(multiplexer_1_out), .Q(Q), .preset(1'b0), .en(1'b1), .reset(CLR));  // open: Qn
endmodule

module REG (
  input  [3:0] Data_i,
  input  CLR,
  input  E,
  input  CLK,
  output [3:0] out_5,
  output [3:0] Data_o
);

  D_E d_e_1 (.in_1(CLK), .D(Data_i[3]), .E(E), .Q(Data_o[3]), .CLR(CLR));
  D_E d_e_2 (.in_1(CLK), .D(Data_i[2]), .E(E), .Q(Data_o[2]), .CLR(CLR));
  D_E d_e_3 (.in_1(CLK), .D(Data_i[1]), .E(E), .Q(Data_o[1]), .CLR(CLR));
  D_E d_e_4 (.in_1(CLK), .D(Data_i[0]), .E(E), .Q(Data_o[0]), .CLR(CLR));

  assign out_5 = Data_o;
endmodule

module RAM (
  input  ld,
  input  [2:0] A0_2,
  input  str,
  input  Sel,
  input  [3:0] D0_3,
  input  CLK,
  output [3:0] D0_3_2
);

  wire and_1_out, decoder_1_out0, decoder_1_out1, decoder_1_out2, decoder_1_out3, decoder_1_out4,
       decoder_1_out5, decoder_1_out6, decoder_1_out7;
  wire [3:0] reg_1_data_o, reg_2_data_o, reg_3_data_o, reg_4_data_o, reg_5_data_o, reg_6_data_o,
       reg_7_data_o, reg_8_data_o;

  and and_1 (and_1_out, str, Sel);
  Decoder #(.select(3), .disabled(0)) decoder_1 (
    .out0(decoder_1_out0), .out1(decoder_1_out1), .out2(decoder_1_out2), .out3(decoder_1_out3),
    .out4(decoder_1_out4), .out5(decoder_1_out5), .out6(decoder_1_out6), .out7(decoder_1_out7), .sel(A0_2),
    .en(and_1_out));
  REG reg_1 (.Data_i(D0_3), .E(decoder_1_out0), .CLK(CLK), .Data_o(reg_1_data_o));  // open: CLR, out_5
  REG reg_2 (.Data_i(D0_3), .E(decoder_1_out1), .CLK(CLK), .Data_o(reg_2_data_o));  // open: CLR, out_5
  REG reg_3 (.Data_i(D0_3), .E(decoder_1_out2), .CLK(CLK), .Data_o(reg_3_data_o));  // open: CLR, out_5
  REG reg_4 (.Data_i(D0_3), .E(decoder_1_out3), .CLK(CLK), .Data_o(reg_4_data_o));  // open: CLR, out_5
  REG reg_5 (.Data_i(D0_3), .E(decoder_1_out4), .CLK(CLK), .Data_o(reg_5_data_o));  // open: CLR, out_5
  REG reg_6 (.Data_i(D0_3), .E(decoder_1_out5), .CLK(CLK), .Data_o(reg_6_data_o));  // open: CLR, out_5
  REG reg_7 (.Data_i(D0_3), .E(decoder_1_out6), .CLK(CLK), .Data_o(reg_7_data_o));  // open: CLR, out_5
  REG reg_8 (.Data_i(D0_3), .E(decoder_1_out7), .CLK(CLK), .Data_o(reg_8_data_o));  // open: CLR, out_5
  // Probe on reg_1_data_o
  // Probe on reg_2_data_o
  // Probe on reg_3_data_o
  // Probe on reg_4_data_o
  // Probe on reg_5_data_o
  // Probe on reg_6_data_o
  // Probe on reg_7_data_o
  // Probe on reg_8_data_o
  Multiplexer #(.select(3), .width(4)) multiplexer_1 (
    .in0(reg_1_data_o), .in1(reg_2_data_o), .in2(reg_3_data_o), .in3(reg_4_data_o), .in4(reg_5_data_o),
    .in5(reg_6_data_o), .in6(reg_7_data_o), .in7(reg_8_data_o), .out(D0_3_2), .sel(A0_2), .en(ld));

  // Notes on the sheet:
  //   0
  //   1
  //   2
  //   3
  //   4
  //   5
  //   6
  //   7
endmodule
