// Logisim project core3.circ as structural Verilog: 10 circuits, main circuit Unidade Processamento
module Unidade_Processamento (
  input  [3:0] Data_in,
  input  [3:0] IMM4,
  input  [1:0] SD,
  input  [1:0] AD,
  input  ER,
  input  [1:0] AA,
  input  [1:0] AB,
  input  SnA,
  input  EP,
  input  CLK,
  output [3:0] Address,
  output [3:0] Data_out,
  output C
);

  wire alu_1_cybw;
  wire [3:0] alu_1_r, multiplexer_1_out, register_file_1_out_7, register_file_1_out_8, register_file_1_out_9,
       register_file_1_out_10;

  Multiplexer #(.select(2), .width(4), .enable("false")) multiplexer_1 (
    .in0(IMM4), .in1(Data_in), .in2(alu_1_r), .out(multiplexer_1_out), .sel(SD));  // open: in3
  // Probe on register_file_1_out_10
  // Probe on register_file_1_out_9
  // Probe on register_file_1_out_8
  Register_File register_file_1 (
    .in_1(multiplexer_1_out), .CLK(CLK), .ER(ER), .AD(AD), .AA(AA), .AB(AB), .A(Data_out), .B(Address),
    .out_10(register_file_1_out_10), .out_9(register_file_1_out_9), .out_8(register_file_1_out_8),
    .out_7(register_file_1_out_7));
  // Probe on register_file_1_out_7
  Register #(.width(1)) register_1 (.D(alu_1_cybw), .en(EP), .Q(C), .clk(CLK), .clr(1'b1));
  ALU alu_1 (.A(Data_out), .B(Address), .SnA(SnA), .R(alu_1_r), .CyBw(alu_1_cybw));  // open: Z
endmodule

module Unidade_Controlo (
  input  Reset,
  input  MCLK,
  input  C,
  input  [8:0] instruction,
  output [4:0] CodeAddr,
  output [3:0] imm4,
  output [1:0] AB,
  output [1:0] AA,
  output [1:0] AD,
  output [1:0] SD,
  output ER,
  output EP,
  output SnA,
  output WR,
  output RD
);

  wire not_1_out, SO;
  wire [4:0] adder_1_out_3, multiplexer_1_out, Offset5;

  Multiplexer #(.width(5), .enable("false")) multiplexer_1 (
    .in0(5'b00001), .in1(Offset5), .out(multiplexer_1_out), .sel(SO));
  ADDER adder_1 (.in_1(multiplexer_1_out), .in_2(CodeAddr), .out_3(adder_1_out_3));
  not not_1 (not_1_out, MCLK);
  PC pc_1 (.Data_i(adder_1_out_3), .CLR(Reset), .E(1'b1), .CLK(not_1_out), .Data_o(CodeAddr));
  Instruction_Decoder instruction_decoder_1 (
    .\Instrução (instruction), .Offset5(Offset5), .AD(AD), .SD(SD), .ER(ER), .EP(EP), .SnA(SnA), .SO(SO),
    .WR(WR), .C(C), .RD(RD), .Immediate4(imm4), .AA(AA), .AB(AB));

  // Notes on the sheet:
  //   PC
endmodule

module Register_File (
  input  [3:0] in_1,
  input  CLK,
  input  [1:0] AD,
  input  ER,
  input  [1:0] AB,
  input  [1:0] AA,
  output [3:0] out_7,
  output [3:0] out_8,
  output [3:0] out_9,
  output [3:0] out_10,
  output [3:0] A,
  output [3:0] B
);

  wire decoder_1_out0, decoder_1_out1, decoder_1_out2, decoder_1_out3;

  Decoder #(.select(2), .disabled(0)) decoder_1 (
    .out0(decoder_1_out0), .out1(decoder_1_out1), .out2(decoder_1_out2), .out3(decoder_1_out3), .sel(AD),
    .en(ER));
  REG reg_1 (.Data_i(in_1), .CLR(1'b0), .E(decoder_1_out0), .CLK(CLK), .Data_o(out_10));
  Multiplexer #(.select(2), .width(4), .disabled(0), .enable("false")) multiplexer_1 (
    .in0(out_10), .in1(out_9), .in2(out_8), .in3(out_7), .out(A), .sel(AA));
  REG reg_2 (.Data_i(in_1), .CLR(1'b0), .E(decoder_1_out1), .CLK(CLK), .Data_o(out_9));
  REG reg_3 (.Data_i(in_1), .CLR(1'b0), .E(decoder_1_out2), .CLK(CLK), .Data_o(out_8));
  Multiplexer #(.select(2), .width(4), .disabled(0), .enable("false")) multiplexer_2 (
    .in0(out_10), .in1(out_9), .in2(out_8), .in3(out_7), .out(B), .sel(AB));
  REG reg_4 (.Data_i(in_1), .CLR(1'b0), .E(decoder_1_out3), .CLK(CLK), .Data_o(out_7));
endmodule

module Instruction_Decoder (
  input  [8:0] \Instrução ,
  input  C,
  output [3:0] Immediate4,
  output [4:0] Offset5,
  output [1:0] AB,
  output [1:0] AA,
  output [1:0] AD,
  output [1:0] SD,
  output ER,
  output EP,
  output SnA,
  output SO,
  output WR,
  output RD
);

  ROM #(.addrWidth(4)) rom_1 (.addr({\Instrução [8:6], C}), .data({SD, ER, EP, SnA, SO, WR, RD}), .sel(1'b1));

  assign AA = \Instrução [3:2];
  assign AB = \Instrução [1:0];
  assign AD = \Instrução [5:4];
  assign Immediate4 = \Instrução [3:0];
  assign Offset5 = \Instrução [4:0];

  // Notes on the sheet:
  //   contents of rom_1 (hex, n*v repeats v):
  //   20 20 61 61 2 2 b8 b8 b0 b0 4 0 4 4 18 18
endmodule

module CPU (
);

  wire alu_1_cybw, CLK, EP, ER, not_1_out, or_1_out, PSW_q, RD, Reset_out, SnA, SO, WR;
  wire [1:0] AA, AB, AD, SD;
  wire [3:0] alu_1_r, imm4, multiplexer_2_out, ram_1_data, register_file_1_a, register_file_1_b,
       register_file_1_out_7, register_file_1_out_8, register_file_1_out_9, register_file_1_out_10;
  wire [4:0] adder_1_out_3, multiplexer_1_out, offset5, pc_1_data_o;
  wire [8:0] rom_1_data;

  Button Reset (.out(Reset_out));
  Clock MCLK (.out(CLK));
  Multiplexer #(.width(5), .enable("false")) multiplexer_1 (
    .in0(5'b00001), .in1(offset5), .out(multiplexer_1_out), .sel(SO));
  ADDER adder_1 (.in_1(multiplexer_1_out), .in_2(pc_1_data_o), .out_3(adder_1_out_3));
  not not_1 (not_1_out, CLK);
  PC pc_1 (.Data_i(adder_1_out_3), .CLR(Reset_out), .E(1'b1), .CLK(not_1_out), .Data_o(pc_1_data_o));
  // Probe on pc_1_data_o
  // Probe on rom_1_data
  ROM #(.addrWidth(5), .dataWidth(9)) rom_1 (.addr(pc_1_data_o), .data(rom_1_data), .sel(1'b1));
  Instruction_Decoder instruction_decoder_1 (
    .\Instrução (rom_1_data), .Offset5(offset5), .AD(AD), .SD(SD), .ER(ER), .EP(EP), .SnA(SnA), .SO(SO),
    .WR(WR), .C(PSW_q), .RD(RD), .Immediate4(imm4), .AA(AA), .AB(AB));
  // Probe on AD
  // Probe on SD
  Multiplexer #(.select(2), .width(4), .disabled(0), .enable("false")) multiplexer_2 (
    .in0(imm4), .in1(ram_1_data), .in2(alu_1_r), .out(multiplexer_2_out), .sel(SD));  // open: in3
  // Probe on multiplexer_2_out
  // Probe on register_file_1_out_10
  // Probe on register_file_1_out_9
  // Probe on register_file_1_out_8
  Register_File register_file_1 (
    .in_1(multiplexer_2_out), .CLK(CLK), .ER(ER), .AD(AD), .AA(AA), .AB(AB), .A(register_file_1_a),
    .B(register_file_1_b), .out_10(register_file_1_out_10), .out_9(register_file_1_out_9),
    .out_8(register_file_1_out_8), .out_7(register_file_1_out_7));
  // Probe on register_file_1_out_7
  Register #(.width(1)) PSW (.D(alu_1_cybw), .en(EP), .Q(PSW_q), .clk(CLK));  // open: clr
  ALU alu_1 (.A(register_file_1_a), .B(register_file_1_b), .SnA(SnA), .R(alu_1_r), .CyBw(alu_1_cybw));  // open: Z
  // Probe on register_file_1_b
  // Probe on register_file_1_a
  // Probe on PSW_q
  or or_1 (or_1_out, WR, RD);
  RAM #(.addrWidth(4), .dataWidth(4), .bus("separate")) ram_1 (
    .addr(register_file_1_b), .din(register_file_1_a), .data(ram_1_data), .str(WR), .sel(or_1_out),
    .clk(CLK), .ld(RD), .clr(1'b0));

  // Notes on the sheet:
  //   PC
  //   Code memory
  //   contents of rom_1 (hex, n*v repeats v):
  //   1a 41 1b 61 1c2 143 1c 89 183 1c 81 180
  //   Data memory
endmodule

module ALU (
  input  [3:0] A,
  input  [3:0] B,
  input  SnA,
  output [3:0] R,
  output Z,
  output CyBw
);

  wire adder_1_cout, subtractor_1_bout;
  wire [3:0] adder_1_out, subtractor_1_out;

  Subtractor #(.width(4)) subtractor_1 (.a(A), .b(B), .out(subtractor_1_out), .bin(1'b0), .bout(subtractor_1_bout));
  Adder #(.width(4)) adder_1 (.a(A), .b(B), .out(adder_1_out), .cin(1'b0), .cout(adder_1_cout));
  Multiplexer #(.disabled(0), .enable("false")) multiplexer_1 (
    .in0(adder_1_cout), .in1(subtractor_1_bout), .out(CyBw), .sel(SnA));
  Multiplexer #(.width(4), .disabled(0), .enable("false")) multiplexer_2 (
    .in0(adder_1_out), .in1(subtractor_1_out), .out(R), .sel(SnA));
  and and_1 (Z, ~R[0], ~R[1], ~R[2], ~R[3]);  // AND_Gate
endmodule

module D_E (
  input  in_1,
  input  D,
  input  E,
  input  CLR,
  output Q
);

  wire multiplexer_1_out;

  Multiplexer #(.disabled(0), .enable("false")) multiplexer_1 (.in0(Q), .in1(D), .out(multiplexer_1_out), .sel(E));
  D_Flip_Flop d_ff_1 (.clk(in_1), .D(multiplexer_1_out), .Q(Q), .preset(1'b0), .en(1'b1), .reset(CLR));  // open: Qn
endmodule

module REG (
  input  [3:0] Data_i,
  input  CLR,
  input  E,
  input  CLK,
  output [3:0] Data_o
);

  D_E d_e_1 (.in_1(CLK), .D(Data_i[3]), .E(E), .CLR(CLR), .Q(Data_o[3]));
  D_E d_e_2 (.in_1(CLK), .D(Data_i[2]), .E(E), .CLR(CLR), .Q(Data_o[2]));
  D_E d_e_3 (.in_1(CLK), .D(Data_i[1]), .E(E), .CLR(CLR), .Q(Data_o[1]));
  D_E d_e_4 (.in_1(CLK), .D(Data_i[0]), .E(E), .CLR(CLR), .Q(Data_o[0]));
endmodule

module ADDER (
  input  [4:0] in_1,
  input  [4:0] in_2,
  output [4:0] out_3
);

  Adder #(.width(5)) adder_1 (.a(in_1), .b(in_2), .out(out_3), .cin(1'b0));  // open: cout
endmodule

module PC (
  input  [4:0] Data_i,
  input  CLR,
  input  E,
  input  CLK,
  output [4:0] Data_o
);

  D_E d_e_1 (.in_1(CLK), .D(Data_i[4]), .E(E), .CLR(CLR), .Q(Data_o[4]));
  D_E d_e_2 (.in_1(CLK), .D(Data_i[3]), .E(E), .CLR(CLR), .Q(Data_o[3]));
  D_E d_e_3 (.in_1(CLK), .D(Data_i[2]), .E(E), .CLR(CLR), .Q(Data_o[2]));
  D_E d_e_4 (.in_1(CLK), .D(Data_i[1]), .E(E), .CLR(CLR), .Q(Data_o[1]));
  D_E d_e_5 (.in_1(CLK), .D(Data_i[0]), .E(E), .CLR(CLR), .Q(Data_o[0]));
endmodule
