// Logisim project p4b.circ as structural Verilog: 10 circuits, main circuit Register File
module micro (
  output [3:0] out_1
);

  wire alu_1_cybw, CLK, EF, ER, flags, not_1_out, not_2_out, OP_ALU, or_1_out, RD, Reset_out, SC, SO, WR;
  wire [1:0] AA, AB, AD, const2, SD;
  wire [3:0] alu_1_r, controlled_buffer_1_out, imm4, multiplexer_2_out, multiplexer_3_out, register_file_1_a,
       register_file_1_out_7, register_file_1_out_8, register_file_1_out_9, register_file_1_out_10,
       zerofill4_1_out_2;
  wire [5:0] offset6;
  wire [7:0] adder_1_out_3, multiplexer_1_out, pc_1_data_o, signfill8_1_out_2;
  wire [8:0] rom_1_data;

  Button Reset (.out(Reset_out));
  Clock MCLK (.out(CLK));
  Multiplexer #(.width(8), .enable("false")) multiplexer_1 (
    .in0(8'h1), .in1(signfill8_1_out_2), .out(multiplexer_1_out), .sel(SO));
  ADDER adder_1 (.in_1(multiplexer_1_out), .in_2(pc_1_data_o), .out_3(adder_1_out_3));
  not not_1 (not_1_out, CLK);
  signFill8 signfill8_1 (.in_1(offset6), .out_2(signfill8_1_out_2));
  PC pc_1 (.Data_i(adder_1_out_3), .CLR(Reset_out), .E(1'b1), .CLK(not_1_out), .Data_o(pc_1_data_o));
  Instruction_Decoder instruction_decoder_1 (
    .\Instrução (rom_1_data), .offset6(offset6), .AD(AD), .SD(SD), .SC(SC), .OP_ALU(OP_ALU), .EF(EF),
    .SO(SO), .RD(RD), .C(flags), .WR(WR), .immediate4(imm4), .AB(AB), .AA(AA), .const2(const2), .ER(ER));
  ROM #(.dataWidth(9)) rom_1 (.addr(pc_1_data_o), .data(rom_1_data), .sel(1'b1));
  // Probe on rom_1_data
  // Probe on imm4
  // Probe on SD
  // Probe on AD
  // Probe on ER
  // Probe on AA
  // Probe on AB
  zeroFill4 zerofill4_1 (.in_1(const2), .out_2(zerofill4_1_out_2));
  Multiplexer #(.select(2), .width(4), .disabled(0), .enable("false")) multiplexer_2 (
    .in0(imm4), .in1(controlled_buffer_1_out), .in2(alu_1_r), .out(multiplexer_2_out), .sel(SD));  // open: in3
  // Probe on register_file_1_out_7
  // Probe on register_file_1_out_8
  // Probe on register_file_1_out_9
  // Probe on register_file_1_out_10
  Register_File register_file_1 (
    .in_1(multiplexer_2_out), .CLK(CLK), .ER(ER), .AD(AD), .AA(AA), .AB(AB), .A(register_file_1_a),
    .B(out_1), .out_7(register_file_1_out_7), .out_8(register_file_1_out_8), .out_9(register_file_1_out_9),
    .out_10(register_file_1_out_10));
  Multiplexer #(.width(4), .disabled(0), .enable("false")) multiplexer_3 (
    .in0(zerofill4_1_out_2), .in1(out_1), .out(multiplexer_3_out), .sel(SC));
  ALU alu_1 (.A(register_file_1_a), .B(multiplexer_3_out), .SnA(OP_ALU), .R(alu_1_r), .CyBw(alu_1_cybw));
  Register #(.width(1)) PSW (.D(alu_1_cybw), .en(EF), .Q(flags), .clk(CLK), .clr(1'b0));
  assign controlled_buffer_1_out = WR ? register_file_1_a : 4'bz;  // Controlled_Buffer controlled_buffer_1
  or or_1 (or_1_out, RD, WR);
  RAM #(.addrWidth(4), .dataWidth(4)) ram_1 (
    .addr(out_1), .data(controlled_buffer_1_out), .sel(or_1_out), .clk(CLK), .ld(not_2_out), .clr(1'b0));
  not not_2 (not_2_out, WR);

  // Notes on the sheet:
  //   PC
  //   Memória de Programa
  //   Banco Registos
  //   Memória de Dados
endmodule

module Register_File (
  input  [3:0] in_1,
  input  CLK,
  input  ER,
  input  [1:0] AD,
  input  [1:0] AA,
  input  [1:0] AB,
  output [3:0] out_7,
  output [3:0] out_8,
  output [3:0] out_9,
  output [3:0] out_10,
  output [3:0] A,
  output [3:0] B
);

  wire decoder_1_out0, decoder_1_out1, decoder_1_out2, decoder_1_out3;

  Decoder #(.select(2), .disabled(0)) decoder_1 (
    .out0(decoder_1_out0), .out1(decoder_1_out1), .out2(decoder_1_out2), .out3(decoder_1_out3), .sel(AD),
    .en(ER));
  REG reg_1 (.Data_i(in_1), .CLR(1'b0), .E(decoder_1_out0), .CLK(CLK), .Data_o(out_7));
  Multiplexer #(.select(2), .width(4), .disabled(0), .enable("false")) multiplexer_1 (
    .in0(out_7), .in1(out_8), .in2(out_9), .in3(out_10), .out(A), .sel(AA));
  REG reg_2 (.Data_i(in_1), .CLR(1'b0), .E(decoder_1_out1), .CLK(CLK), .Data_o(out_8));
  REG reg_3 (.Data_i(in_1), .CLR(1'b0), .E(decoder_1_out2), .CLK(CLK), .Data_o(out_9));
  Multiplexer #(.select(2), .width(4), .disabled(0), .enable("false")) multiplexer_2 (
    .in0(out_7), .in1(out_8), .in2(out_9), .in3(out_10), .out(B), .sel(AB));
  REG reg_4 (.Data_i(in_1), .CLR(1'b0), .E(decoder_1_out3), .CLK(CLK), .Data_o(out_10));
endmodule

module Instruction_Decoder (
  input  [8:0] \Instrução ,
  input  C,
  output [3:0] immediate4,
  output [5:0] offset6,
  output [1:0] const2,
  output [1:0] AA,
  output [1:0] AD,
  output [1:0] AB,
  output OP_ALU,
  output [1:0] SD,
  output ER,
  output SC,
  output EF,
  output SO,
  output RD,
  output WR
);

  wire [7:0] rom_1_data;

  ROM #(.addrWidth(4)) rom_1 (.addr({\Instrução [2:0], C}), .data(rom_1_data), .sel(1'b1));
endmodule

module ALU (
  input  [3:0] A,
  input  [3:0] B,
  input  SnA,
  output [3:0] R,
  output CyBw
);

  wire adder_1_cout, subtractor_1_bout;
  wire [3:0] adder_1_out, subtractor_1_out;

  Adder #(.width(4)) adder_1 (.a(A), .b(B), .out(adder_1_out), .cin(1'b0), .cout(adder_1_cout));
  Subtractor #(.width(4)) subtractor_1 (.a(A), .b(B), .out(subtractor_1_out), .bin(1'b0), .bout(subtractor_1_bout));
  Multiplexer #(.disabled(0), .enable("false")) multiplexer_1 (
    .in0(adder_1_cout), .in1(subtractor_1_bout), .out(CyBw), .sel(SnA));
  Multiplexer #(.width(4), .disabled(0), .enable("false")) multiplexer_2 (
    .in0(adder_1_out), .in1(subtractor_1_out), .out(R), .sel(SnA));
endmodule

module PC (
  input  [7:0] Data_i,
  input  CLR,
  input  E,
  input  CLK,
  output [7:0] Data_o
);

  D_E d_e_1 (.in_1(CLK), .D(Data_i[7]), .E(E), .CLR(CLR), .Q(Data_o[7]));
  D_E d_e_2 (.in_1(CLK), .D(Data_i[6]), .E(E), .CLR(CLR), .Q(Data_o[6]));
  D_E d_e_3 (.in_1(CLK), .D(Data_i[5]), .E(E), .CLR(CLR), .Q(Data_o[5]));
  D_E d_e_4 (.in_1(CLK), .D(Data_i[4]), .E(E), .CLR(CLR), .Q(Data_o[4]));
  D_E d_e_5 (.in_1(CLK), .D(Data_i[3]), .E(E), .CLR(CLR), .Q(Data_o[3]));
  D_E d_e_6 (.in_1(CLK), .D(Data_i[2]), .E(E), .CLR(CLR), .Q(Data_o[2]));
  D_E d_e_7 (.in_1(CLK), .D(Data_i[1]), .E(E), .CLR(CLR), .Q(Data_o[1]));
  D_E d_e_8 (.in_1(CLK), .D(Data_i[0]), .E(E), .CLR(CLR), .Q(Data_o[0]));
endmodule

module D_E (
  input  in_1,
  input  D,
  input  E,
  input  CLR,
  output Q
);

  wire multiplexer_1_out;

  Multiplexer #(.disabled(0), .enable("false")) multiplexer_1 (.in0(Q), .in1(D), .out(multiplexer_1_out), .sel(E));
  D_Flip_Flop d_ff_1 (.clk(in_1), .D(multiplexer_1_out), .Q(Q), .preset(1'b0), .en(1'b1), .reset(CLR));  // open: Qn
endmodule

module REG (
  input  [3:0] Data_i,
  input  CLR,
  input  E,
  input  CLK,
  output [3:0] Data_o
);

  D_E d_e_1 (.in_1(CLK), .D(Data_i[3]), .E(E), .CLR(CLR), .Q(Data_o[3]));
  D_E d_e_2 (.in_1(CLK), .D(Data_i[2]), .E(E), .CLR(CLR), .Q(Data_o[2]));
  D_E d_e_3 (.in_1(CLK), .D(Data_i[1]), .E(E), .CLR(CLR), .Q(Data_o[1]));
  D_E d_e_4 (.in_1(CLK), .D(Data_i[0]), .E(E), .CLR(CLR), .Q(Data_o[0]));
endmodule

module ADDER (
  input  [7:0] in_1,
  input  [7:0] in_2,
  output [7:0] out_3
);

  Adder adder_1 (.a(in_1), .b(in_2), .out(out_3), .cin(1'b0));  // open: cout
endmodule

module zeroFill4 (
  input  [1:0] in_1,
  output [3:0] out_2
);


  assign out_2 = {2'b00, in_1};
endmodule

module signFill8 (
  input  [5:0] in_1,
  output [7:0] out_2
);


  assign out_2 = {{3{in_1[5]}}, in_1[4:0]};
endmodule
