// Logisim project cpu_final.circ as structural Verilog: 10 circuits, main circuit register file
module CPU (
);

  wire alu_1_z, EP, ER, MCLK_out, not_1_out, not_2_out, or_1_out, PSR_q, RD, Reset_out, SA, SC, SI, SO, WR;
  wire [1:0] OP_ALU, SD;
  wire [2:0] AA, AB, AD, Const3, interconnections_1_opcode;
  wire [5:0] Const6;
  wire [7:0] alu_1_r, controlled_buffer_1_out, multiplexer_3_out, multiplexer_4_out, multiplexer_5_out,
       Offset8, register_file_1_a, register_file_1_b, register_file_1_r0, register_file_1_r1,
       register_file_1_r2, register_file_1_r3, register_file_1_r4, register_file_1_r5, register_file_1_r6,
       register_file_1_r7, zerofill3_1_d, zerofill6_1_d;
  wire [9:0] adder_1_out, multiplexer_1_out, multiplexer_2_out, PC_q, signext_1_d, zerofill10_1_d;
  wire [11:0] rom_1_data;

  Button Reset (.out(Reset_out));
  Clock MCLK (.out(MCLK_out));
  signExt signext_1 (.A(Offset8), .D(signext_1_d));
  Multiplexer #(.width(10), .enable("false")) multiplexer_1 (
    .in0(10'h1), .in1(signext_1_d), .out(multiplexer_1_out), .sel(SO));
  Adder #(.width(10)) adder_1 (.a(multiplexer_1_out), .b(PC_q), .out(adder_1_out), .cin(1'b0));  // open: cout
  zeroFill10 zerofill10_1 (.A(register_file_1_a), .D(zerofill10_1_d));
  Multiplexer #(.width(10), .disabled(0), .enable("false")) multiplexer_2 (
    .in0(adder_1_out), .in1(zerofill10_1_d), .out(multiplexer_2_out), .sel(SI));
  Register #(.width(10)) PC (.D(multiplexer_2_out), .en(1'b1), .Q(PC_q), .clk(MCLK_out), .clr(Reset_out));
  // Probe on multiplexer_2_out
  // Probe on PC_q
  not not_1 (not_1_out, MCLK_out);
  ROM #(.addrWidth(10), .dataWidth(12)) rom_1 (.addr(PC_q), .data(rom_1_data), .sel(1'b1));
  // Probe on rom_1_data
  Interconnections interconnections_1 (
    .Instruction(rom_1_data), .const3(Const3), .AB(AB), .AA(AA), .AD(AD), .OP_ALU(OP_ALU), .const6(Const6),
    .offset8(Offset8), .opCode(interconnections_1_opcode));
  zeroFill6 zerofill6_1 (.A(Const6), .D(zerofill6_1_d));
  // Probe on SD
  zeroFill3 zerofill3_1 (.A(Const3), .D(zerofill3_1_d));
  Multiplexer #(.select(2), .width(8), .disabled(0), .enable("false")) multiplexer_3 (
    .in0(zerofill6_1_d), .in1(controlled_buffer_1_out), .in2(alu_1_r), .out(multiplexer_3_out), .sel(SD));  // open: in3
  register_file register_file_1 (
    .AD(AD), .ER(ER), .AA(AA), .AB(AB), .clk(not_1_out), .D(multiplexer_3_out), .A(register_file_1_a),
    .B(register_file_1_b), .R0(register_file_1_r0), .R1(register_file_1_r1), .R2(register_file_1_r2),
    .R3(register_file_1_r3), .R4(register_file_1_r4), .R5(register_file_1_r5), .R6(register_file_1_r6),
    .R7(register_file_1_r7));
  ALU alu_1 (.Ci(1'b0), .A(register_file_1_a), .B(multiplexer_4_out), .Z(alu_1_z), .R(alu_1_r), .OP_ALU(OP_ALU));
  // Probe on register_file_1_r0
  // Probe on register_file_1_r1
  // Probe on register_file_1_r2
  // Probe on register_file_1_r3
  // Probe on register_file_1_r4
  // Probe on register_file_1_r5
  // Probe on register_file_1_r6
  // Probe on register_file_1_r7
  Multiplexer #(.width(8), .enable("false")) multiplexer_4 (
    .in0(zerofill3_1_d), .in1(register_file_1_b), .out(multiplexer_4_out), .sel(SC));
  // Probe on alu_1_r
  // Probe on interconnections_1_opcode
  // Probe on multiplexer_5_out
  Multiplexer #(.width(8), .enable("false")) multiplexer_5 (
    .in0(alu_1_r), .in1(register_file_1_b), .out(multiplexer_5_out), .sel(SA));
  assign controlled_buffer_1_out = WR ? register_file_1_a : 8'bz;  // Controlled_Buffer controlled_buffer_1
  Register #(.width(1)) PSR (.D(alu_1_z), .en(EP), .Q(PSR_q), .clk(not_1_out), .clr(1'b0));
  instruction_decoder instruction_decoder_1 (
    .opCode(interconnections_1_opcode), .Z(PSR_q), .RD(RD), .WR(WR), .EP(EP), .ER(ER), .SA(SA), .SC(SC),
    .SD(SD), .SO(SO), .SI(SI));
  // Probe on controlled_buffer_1_out
  not not_2 (not_2_out, WR);
  or or_1 (or_1_out, WR, RD);
  RAM ram_1 (
    .addr(multiplexer_5_out), .data(controlled_buffer_1_out), .sel(or_1_out), .clk(not_1_out),
    .ld(not_2_out), .clr(1'b0));
  // Probe on PSR_q

  // Notes on the sheet:
  //   Code memory
  //   contents of rom_1 (hex, n*v repeats v):
  //   600 640 684 701 8c0 4b 4 202 a10 44a e0a c00
  //   Data memory
endmodule

module register_file (
  input  [7:0] D,
  input  ER,
  input  [2:0] AD,
  input  clk,
  input  [2:0] AA,
  input  [2:0] AB,
  output [7:0] R0,
  output [7:0] R1,
  output [7:0] R2,
  output [7:0] R3,
  output [7:0] R4,
  output [7:0] R5,
  output [7:0] R6,
  output [7:0] R7,
  output [7:0] A,
  output [7:0] B
);

  wire decoder_1_out0, decoder_1_out1, decoder_1_out2, decoder_1_out3, decoder_1_out4, decoder_1_out5,
       decoder_1_out6, decoder_1_out7;

  Decoder #(.select(3), .disabled(0)) decoder_1 (
    .out0(decoder_1_out0), .out1(decoder_1_out1), .out2(decoder_1_out2), .out3(decoder_1_out3),
    .out4(decoder_1_out4), .out5(decoder_1_out5), .out6(decoder_1_out6), .out7(decoder_1_out7), .sel(AD),
    .en(ER));
  Register u_R0 (.D(D), .en(decoder_1_out0), .Q(R0), .clk(clk));  // open: clr
  Register u_R1 (.D(D), .en(decoder_1_out1), .Q(R1), .clk(clk));  // open: clr
  Multiplexer #(.select(3), .width(8), .disabled(0), .enable("false")) multiplexer_1 (
    .in0(R0), .in1(R1), .in2(R2), .in3(R3), .in4(R4), .in5(R5), .in6(R6), .in7(R7), .out(A), .sel(AA));
  Register u_R2 (.D(D), .en(decoder_1_out2), .Q(R2), .clk(clk));  // open: clr
  Register u_R3 (.D(D), .en(decoder_1_out3), .Q(R3), .clk(clk));  // open: clr
  Register u_R4 (.D(D), .en(decoder_1_out4), .Q(R4), .clk(clk));  // open: clr
  Register u_R5 (.D(D), .en(decoder_1_out5), .Q(R5), .clk(clk));  // open: clr
  Register u_R6 (.D(D), .en(decoder_1_out6), .Q(R6), .clk(clk));  // open: clr
  Multiplexer #(.select(3), .width(8), .disabled(0), .enable("false")) multiplexer_2 (
    .in0(R0), .in1(R1), .in2(R2), .in3(R3), .in4(R4), .in5(R5), .in6(R6), .in7(R7), .out(B), .sel(AB));
  Register u_R7 (.D(D), .en(decoder_1_out7), .Q(R7), .clk(clk));  // open: clr
endmodule

module instruction_decoder (
  input  Z,
  input  [2:0] opCode,
  output RD,
  output WR,
  output EP,
  output ER,
  output SA,
  output SC,
  output [1:0] SD,
  output SO,
  output SI
);

  ROM #(.addrWidth(4), .dataWidth(10)) rom_1 (
    .addr({opCode, Z}), .data({SI, SO, SD, SC, SA, ER, EP, WR, RD}), .sel(1'b1));

  // Notes on the sheet:
  //   contents of rom_1 (hex, n*v repeats v):
  //   ac ac 24 24 8c 8c 8 8 49 49 200 0 100 100 12 12
endmodule

module ALU (
  input  Ci,
  input  [7:0] A,
  input  [7:0] B,
  input  [1:0] OP_ALU,
  output Z,
  output [7:0] R
);

  wire xor_1_out;
  wire [7:0] adder_1_out, barrelsh_1_y, bit_extender_1_out, multiplexer_1_out, or_1_out, xor_2_out;

  assign bit_extender_1_out = {{7{OP_ALU[0]}}, OP_ALU[0]};  // Bit_Extender bit_extender_1
  xor xor_1 (xor_1_out, Ci, OP_ALU[0]);
  assign xor_2_out = B ^ bit_extender_1_out;  // XOR_Gate xor_2, 8 bits wide
  barrelSH barrelsh_1 (.D(A), .S(B[2:0]), .Y(barrelsh_1_y));
  assign or_1_out = A | B;  // OR_Gate or_1, 8 bits wide
  Adder adder_1 (.a(A), .b(xor_2_out), .out(adder_1_out), .cin(xor_1_out));  // open: cout
  Multiplexer #(.width(8), .enable("false")) multiplexer_1 (
    .in0(barrelsh_1_y), .in1(or_1_out), .out(multiplexer_1_out), .sel(OP_ALU[0]));
  Multiplexer #(.width(8), .enable("false")) multiplexer_2 (
    .in0(adder_1_out), .in1(multiplexer_1_out), .out(R), .sel(OP_ALU[1]));
  and and_1 (Z, ~R[0], ~R[1], ~R[2], ~R[3], ~R[4], ~R[5], ~R[6], ~R[7]);  // AND_Gate
endmodule

module barrelSH (
  input  [7:0] D,
  input  [2:0] S,
  output [7:0] Y
);

  Multiplexer #(.select(3), .enable("false")) multiplexer_1 (
    .in0(D[0]), .in1(D[1]), .in2(D[2]), .in3(D[3]), .in4(D[4]), .in5(D[5]), .in6(D[6]), .in7(D[7]),
    .out(Y[0]), .sel(S));
  Multiplexer #(.select(3), .enable("false")) multiplexer_2 (
    .in0(D[1]), .in1(D[2]), .in2(D[3]), .in3(D[4]), .in4(D[5]), .in5(D[6]), .in6(D[7]), .in7(1'b0),
    .out(Y[1]), .sel(S));
  Multiplexer #(.select(3), .enable("false")) multiplexer_3 (
    .in0(D[2]), .in1(D[3]), .in2(D[4]), .in3(D[5]), .in4(D[6]), .in5(D[7]), .in6(1'b0), .in7(1'b0),
    .out(Y[2]), .sel(S));
  Multiplexer #(.select(3), .enable("false")) multiplexer_4 (
    .in0(D[3]), .in1(D[4]), .in2(D[5]), .in3(D[6]), .in4(D[7]), .in5(1'b0), .in6(1'b0), .in7(1'b0),
    .out(Y[3]), .sel(S));
  Multiplexer #(.select(3), .enable("false")) multiplexer_5 (
    .in0(D[4]), .in1(D[5]), .in2(D[6]), .in3(D[7]), .in4(1'b0), .in5(1'b0), .in6(1'b0), .in7(1'b0),
    .out(Y[4]), .sel(S));
  Multiplexer #(.select(3), .enable("false")) multiplexer_6 (
    .in0(D[5]), .in1(D[6]), .in2(D[7]), .in3(1'b0), .in4(1'b0), .in5(1'b0), .in6(1'b0), .in7(1'b0),
    .out(Y[5]), .sel(S));
  Multiplexer #(.select(3), .enable("false")) multiplexer_7 (
    .in0(D[6]), .in1(D[7]), .in2(1'b0), .in3(1'b0), .in4(1'b0), .in5(1'b0), .in6(1'b0), .in7(1'b0),
    .out(Y[6]), .sel(S));
  Multiplexer #(.select(3), .enable("false")) multiplexer_8 (
    .in0(D[7]), .in1(1'b0), .in2(1'b0), .in3(1'b0), .in4(1'b0), .in5(1'b0), .in6(1'b0), .in7(1'b0),
    .out(Y[7]), .sel(S));
endmodule

module Interconnections (
  input  [11:0] Instruction,
  output [2:0] const3,
  output [2:0] AB,
  output [2:0] AA,
  output [2:0] AD,
  output [1:0] OP_ALU,
  output [5:0] const6,
  output [7:0] offset8,
  output [2:0] opCode
);


  assign AA = Instruction[5:3];
  assign AB = Instruction[2:0];
  assign AD = Instruction[8:6];
  assign const3 = Instruction[2:0];
  assign const6 = Instruction[5:0];
  assign offset8 = Instruction[7:0];
  assign OP_ALU = Instruction[10:9];
  assign opCode = Instruction[11:9];
endmodule

module zeroFill6 (
  input  [5:0] A,
  output [7:0] D
);


  assign D = {2'b00, A};
endmodule

module zeroFill3 (
  input  [2:0] A,
  output [7:0] D
);


  assign D = {{5{1'b0}}, A};
endmodule

module signExt (
  input  [7:0] A,
  output [9:0] D
);


  assign D = {{3{A[7]}}, A[6:0]};
endmodule

module zeroFill10 (
  input  [7:0] A,
  output [9:0] D
);


  assign D = {2'b00, A};
endmodule
